# Fritzing sketch sample_schematics (saved by Fritzing 0.9.3b)
breadboards: 2

parts:
  Part1 = Arduino Nano (Rev3.0)
  Part2 = NRF24L01+ Breakout Board
  U1 = 74HC595 [package="DIP16 [THT]"]
  U2 = 74HC595 [package="DIP16 [THT]"]
  Part3 = Solid State High Level Relay Module [package=relay]
  Part4 = Solid State High Level Relay Module [package=relay]
  Part5 = Solid State High Level Relay Module [package=relay]
  Part6 = Solid State High Level Relay Module [package=relay]
  Part7 = Solid State High Level Relay Module [package=relay]
  Part8 = Solid State High Level Relay Module [package=relay]
  Part9 = Solid State High Level Relay Module [package=relay]
  Part10 = Solid State High Level Relay Module [package=relay]
  Part11 = Solid State High Level Relay Module [package=relay]
  Part12 = Solid State High Level Relay Module [package=relay]
  Part13 = Solid State High Level Relay Module [package=relay]
  Part14 = Solid State High Level Relay Module [package=relay]
  Part15 = Solid State High Level Relay Module [package=relay]
  Part16 = Solid State High Level Relay Module [package=relay]
  Part17 = Solid State High Level Relay Module [package=relay]
  Part18 = Solid State High Level Relay Module [package=relay]
  Part19 = Arduino Nano (Rev3.0)
  Part20 = NRF24L01+ Breakout Board
  Part21 = Arduino Nano (Rev3.0)
  Part22 = NRF24L01+ Breakout Board
  U3 = 74HC595 [package="DIP16 [THT]"]
  Part25 = Solid State High Level Relay Module [package=relay]
  Part28 = Solid State High Level Relay Module [package=relay]
  Part29 = Solid State High Level Relay Module [package=relay]
  Part30 = Solid State High Level Relay Module [package=relay]
  Part32 = Solid State High Level Relay Module [package=relay]
  Part35 = Solid State High Level Relay Module [package=relay]
  Part36 = Solid State High Level Relay Module [package=relay]
  Part37 = Solid State High Level Relay Module [package=relay]
  Part38 = Arduino Nano (Rev3.0)
  Part39 = NRF24L01+ Breakout Board
  Part41 = Solid State High Level Relay Module [package=relay]
  Part43 = Solid State High Level Relay Module [package=relay]
  Part45 = Solid State High Level Relay Module [package=relay]
  Part46 = Solid State High Level Relay Module [package=relay]
  U4 = Power Outlet [chip_label=IC package="SIP (Single Inline) [THT]"]  # not connected

nets:
  GND: Part1.GND, Part2.GND, U1.GND, U1.OE, U2.GND, U2.OE, Part3.DC-, Part4.DC-, Part5.DC-, Part6.DC-, Part7.DC-, Part8.DC-, Part9.DC-, Part10.DC-, Part11.DC-, Part12.DC-, Part13.DC-, Part14.DC-, Part15.DC-, Part16.DC-, Part17.DC-, Part18.DC-
  N1: Part1.D2, U1.ST_CP, U2.ST_CP
  N2: Part1.D3, U1.DS
  N3: Part1.D4, U1.SH_CP, U2.SH_CP
  N4: Part1.D9, Part2.CE
  N5: Part1.D10, Part2.CS
  N6: Part1.D11/MOSI, Part2.MOSI
  N7: Part1.D12/MISO, Part2.MISO
  VCC: Part1.5V, U1.MR, U1.VCC, U2.MR, U2.VCC, Part3.DC+, Part4.DC+, Part5.DC+, Part6.DC+, Part7.DC+, Part8.DC+, Part9.DC+, Part10.DC+, Part11.DC+, Part12.DC+, Part13.DC+, Part14.DC+, Part15.DC+, Part16.DC+, Part17.DC+, Part18.DC+
  3V3: Part1.3V3, Part2.VCC
  N8: Part1.D13/SCK, Part2.SCK
  N9: U1.Q1, Part4.CH1
  N10: U1.Q2, Part6.CH1
  N11: U1.Q3, Part5.CH1
  N12: U1.Q4, Part8.CH1
  N13: U1.Q5, Part10.CH1
  N14: U1.Q6, Part9.CH1
  N15: U1.Q7, Part7.CH1
  N16: U1.Q7', U2.DS
  N17: U1.Q0, Part3.CH1
  N18: U2.Q1, Part14.CH1
  N19: U2.Q2, Part16.CH1
  N20: U2.Q3, Part13.CH1
  N21: U2.Q4, Part11.CH1
  N22: U2.Q5, Part18.CH1
  N23: U2.Q6, Part15.CH1
  N24: U2.Q7, Part17.CH1
  N25: U2.Q0, Part12.CH1
  GND_2: Part19.GND, Part20.GND
  N26: Part19.D9, Part20.CE
  N27: Part19.D10, Part20.CS
  N28: Part19.D11/MOSI, Part20.MOSI
  N29: Part19.D12/MISO, Part20.MISO
  3V3_2: Part19.3V3, Part20.VCC
  N30: Part19.D13/SCK, Part20.SCK
  GND_3: Part21.GND, Part21.RESET, Part22.GND, U3.GND, U3.OE, Part25.DC-, Part28.DC-, Part29.DC-, Part30.DC-, Part32.DC-, Part35.DC-, Part36.DC-, Part37.DC-
  N31: Part21.D2, U3.ST_CP
  N32: Part21.D3, U3.DS
  N33: Part21.D4, Part21.D5, U3.SH_CP
  N34: Part21.D9, Part22.CE
  N35: Part21.D10, Part22.CS
  N36: Part21.D11/MOSI, Part22.MOSI
  N37: Part21.D12/MISO, Part22.MISO
  5V: Part21.5V, Part21.A7, U3.MR, U3.VCC, Part25.DC+, Part28.DC+, Part29.DC+, Part30.DC+, Part32.DC+, Part35.DC+, Part36.DC+, Part37.DC+
  3V3_3: Part21.3V3, Part22.VCC
  N38: Part21.D13/SCK, Part22.SCK
  N39: U3.Q1, Part32.CH1
  N40: U3.Q2, Part30.CH1
  N41: U3.Q3, Part29.CH1
  N42: U3.Q4, Part35.CH1
  N43: U3.Q5, Part28.CH1
  N44: U3.Q6, Part36.CH1
  N45: U3.Q7, Part37.CH1
  N46: U3.Q0, Part25.CH1
  GND_4: Part38.GND, Part39.GND, Part41.DC-, Part43.DC-, Part45.DC-, Part46.DC-
  N47: Part38.D2, Part41.CH1
  N48: Part38.D3, Part46.CH1
  N49: Part38.D4, Part45.CH1
  N50: Part38.D5, Part38.D6, Part43.CH1
  N51: Part38.D9, Part39.CE
  N52: Part38.D10, Part39.CS
  N53: Part38.D11/MOSI, Part39.MOSI
  N54: Part38.D12/MISO, Part39.MISO
  N55: Part38.5V, Part41.DC+, Part43.DC+, Part45.DC+, Part46.DC+
  3V3_4: Part38.3V3, Part39.VCC
  N56: Part38.D13/SCK, Part39.SCK

notes:
  Transmitter
  16 channel controller
  8 channel controller
  4 channel controller
  Outlet part source:
  http://fritzing.org/forum/thread/4095/

custom parts:
  Solid State High Level Relay Module: 5V Omron solid state relay 240V 2A output with resistance fuse.
  Power Outlet: A standard power outlet. Silver screws are neutral, brass screws are hot. Green screw is ground.
